# Fritzing sketch sharespresso (saved by Fritzing 0.9.2b)

parts:
  RFID-Reader = RFID-RC522-v2
  Bluetooth = Bluetooth HC-05 Macho
  LCM1602_IIC1 = LCM1602 IIC [part_number="LCM1602 IIC" chip_label="LCM1602 IIC" package="DIP (Dual Inline) [THT]"]
  Kaffeeautomat = mystery part, 3 pins [chip_label=?]
  Bauteil2 = Arduino Uno (Rev3) - ICSP
  LC-Display = LCD screen  # not connected

nets:
  N1: RFID-Reader.SDA, Bauteil2.D9_PWM
  N2: RFID-Reader.SCK, Bauteil2.D13/SCK
  N3: RFID-Reader.MOSI, Bauteil2.D11_PWM/MOSI
  N4: RFID-Reader.MISO, Bauteil2.D12/MISO
  GND: RFID-Reader.GND, Bluetooth.GND, LCM1602_IIC1.GND, Kaffeeautomat.pin2, Bauteil2.GND
  N5: RFID-Reader.RST, Bauteil2.D8
  3.3V: RFID-Reader.3.3V, Bauteil2.3V3
  N6: Bluetooth.TXD, Bauteil2.D6_PWM
  N7: Bluetooth.RXD, Bauteil2.D7
  VCC: Bluetooth.VCC, LCM1602_IIC1.VCC, Bauteil2.5V
  N8: LCM1602_IIC1.SDA, Bauteil2.A4/SDA
  N9: LCM1602_IIC1.SCL, Bauteil2.A5/SCL
  N10: Kaffeeautomat.pin1, Bauteil2.D4
  N11: Kaffeeautomat.pin3, Bauteil2.D5_PWM

custom parts:
  RFID-RC522-v2: A simple China made RFID-RC522 Reader; do check the pin labels, as this is a MFRC522 based clone.
  LCM1602 IIC: I2C-Module to use a 1602 or 2004 LCD on with the wire.h libory Serial LCD Modul
